# Fritzing sketch Headtracker (saved by Fritzing 0.9.3b)

parts:
  Nano1 = Arduino Nano v2.3
  MPU9250_MPU-1 = SparkFun IMU Breakout - MPU-9250 [part_number=" SEN-13762"]

nets:
  N1: Nano1.A5, MPU9250_MPU-1.SCL/SCLK
  N2: Nano1.A4, MPU9250_MPU-1.SDA/SDI
  +5V: Nano1.+5V, MPU9250_MPU-1.VDD
  GND: Nano1.GND, MPU9250_MPU-1.GND
