# Fritzing sketch Remote (saved by Fritzing 0.9.3b)
stripboards: 3

parts:
  Nano1 = Arduino Nano v2.3
  MPU9250_MPU-1 = SparkFun IMU Breakout - MPU-9250 [part_number=" SEN-13762"]
  S1 = Pushbutton [package="[SMD]"]
  S2 = Momentary Switch [package=ksa_sealed_tac_switch]
  JP1 = Header 1 [package=1x01_offset]
  JP2 = Header 1 [package=1x01_offset]
  JP3 = Header 1 [package=1x01_offset]
  JP4 = Header 1 [package=1x01_offset]
  JP5 = Header 1 [package=1x01_offset]
  R1 = Resistor [tolerance=±2% resistance=10 package=THT]

nets:
  N1: Nano1.D7, S1.Pin_3, S1.Pin_4, S2.3, S2.4, JP5.1, R1.Pin_1
  N2: Nano1.A5, MPU9250_MPU-1.SCL/SCLK, JP4.1
  N3: Nano1.A4, MPU9250_MPU-1.SDA/SDI, JP3.1
  +5V: Nano1.+5V, MPU9250_MPU-1.VDD, S1.Pin_1, S1.Pin_2, S2.1, S2.2, JP2.1
  GND: Nano1.GND, MPU9250_MPU-1.GND, JP1.1, R1.Pin_0
